# Fritzing sketch Drzewko (saved by Fritzing 0.9.4)
breadboards: 1

parts:
  Arduino_Nano = Arduino Nano (Rev3.0)
  S1 = Pushbutton [package=THT]
  R1 = Resistor [tolerance=±20% resistance=47k package=THT]
  ERROR_LED = LED - 5mm [color="Blue (470nm)" package="5 mm [THT]"]
  R2 = Resistor [tolerance=±5% resistance=4.7k package=THT]
  LCDscreen = LCD screen
  Interfejs_IIC/I2C = PCF8574 [package="DIP16 [THT]"]
  NPN = NPN-Transistor [package="SOT-23 [SMD]"]
  U1 = POT [package=3362u]
  RTC = Real Time Clock Module - DS1307 RTC Breakout Board
  DHT1 = DHT11 Humitidy and Temperature Sensor
  Micro_SD_TF_Card_Adapter_Module = MicroSD Card Module
  photoResistor = PHOTOCELL [package=photocell-kit]
  R4 = Resistor [tolerance=±5% resistance=4.7k package=THT]
  Soil_Humidity_Sensor = Soil Moisture Sensor

nets:
  GND: Arduino_Nano.GND, R1.Pin_1, R2.Pin_1, LCDscreen.VSS, Interfejs_IIC/I2C.A0, Interfejs_IIC/I2C.A1, Interfejs_IIC/I2C.A2, Interfejs_IIC/I2C.GND, NPN.2, U1.E, RTC.GND, DHT1.GND, Micro_SD_TF_Card_Adapter_Module.GND, R4.Pin_0, Soil_Humidity_Sensor.GND
  N1: Arduino_Nano.D2, ERROR_LED.anode
  N2: Arduino_Nano.D4, Micro_SD_TF_Card_Adapter_Module.CS
  N3: Arduino_Nano.D6, S1.leg1, R1.Pin_0
  N4: Arduino_Nano.D9, DHT1.DATA
  N5: Arduino_Nano.D11/MOSI, Micro_SD_TF_Card_Adapter_Module.MOSI
  N6: Arduino_Nano.D12/MISO, Micro_SD_TF_Card_Adapter_Module.MISO
  12V: Arduino_Nano.VIN
  5V: Arduino_Nano.5V, S1.leg0, LCDscreen.VDD, LCDscreen.LED+, Interfejs_IIC/I2C.VCC, U1.A, RTC.5V, DHT1.VDD, Micro_SD_TF_Card_Adapter_Module.VCC, photoResistor.P$2, Soil_Humidity_Sensor.VCC
  N7: Arduino_Nano.A5, Interfejs_IIC/I2C.SCL, RTC.SCL
  N8: Arduino_Nano.A4, Interfejs_IIC/I2C.SDA, RTC.SDA
  N9: Arduino_Nano.A1, photoResistor.P$1, R4.Pin_1
  N10: Arduino_Nano.A0, Soil_Humidity_Sensor.SIG
  N11: Arduino_Nano.D13/SCK, Micro_SD_TF_Card_Adapter_Module.SCK
  N12: ERROR_LED.cathode, R2.Pin_0
  N13: LCDscreen.V0, U1.S
  N14: LCDscreen.RS, Interfejs_IIC/I2C.P6
  N15: LCDscreen.R/W, Interfejs_IIC/I2C.P5
  N16: LCDscreen.E, Interfejs_IIC/I2C.P4
  N17: LCDscreen.DB4, Interfejs_IIC/I2C.P0
  N18: LCDscreen.DB5, Interfejs_IIC/I2C.P1
  N19: LCDscreen.DB6, Interfejs_IIC/I2C.P2
  N20: LCDscreen.DB7, Interfejs_IIC/I2C.P3
  N21: LCDscreen.LED-, NPN.1
  N22: Interfejs_IIC/I2C.P7, NPN.0

notes:
  Kupiony IIC/I2C Interfejs

custom parts:
  DHT11 Humitidy and Temperature Sensor: DHT11 Humidity and Temperature Sensor
  MicroSD Card Module: A common microSD card module.
